// Logisim project hw3.circ as structural Verilog: 5 circuits, main circuit Part 1: 1-bit Full Adder
module Part_1__1_bit_Full_Adder (
  input  CarryIn,
  input  A,
  input  B,
  output Answer,
  output CarryOut
);

  wire and_1_out, and_2_out, xor_1_out;

  xor xor_1 (xor_1_out, A, B);
  and and_1 (and_1_out, A, B);
  xor xor_2 (Answer, CarryIn, xor_1_out);
  and and_2 (and_2_out, CarryIn, xor_1_out);
  or or_1 (CarryOut, and_2_out, and_1_out);

  // Notes on the sheet:
  //   Yea Won Yoon
  //   903076043
endmodule

module Part_2__4_bit_Full_Adder (
  input  CarryIn,
  input  [3:0] A,
  input  [3:0] B,
  output [3:0] out_4,
  output CarryOut
);

  wire part_1_1_bit_full_adder_1_carryout, part_1_1_bit_full_adder_2_carryout,
       part_1_1_bit_full_adder_3_carryout;

  Part_1__1_bit_Full_Adder part_1_1_bit_full_adder_1 (
    .CarryIn(CarryIn), .A(A[0]), .B(B[0]), .Answer(out_4[0]), .CarryOut(part_1_1_bit_full_adder_1_carryout));
  Part_1__1_bit_Full_Adder part_1_1_bit_full_adder_2 (
    .CarryIn(part_1_1_bit_full_adder_1_carryout), .A(A[1]), .B(B[1]), .Answer(out_4[1]),
    .CarryOut(part_1_1_bit_full_adder_2_carryout));
  Part_1__1_bit_Full_Adder part_1_1_bit_full_adder_3 (
    .CarryIn(part_1_1_bit_full_adder_2_carryout), .A(A[2]), .B(B[2]), .Answer(out_4[2]),
    .CarryOut(part_1_1_bit_full_adder_3_carryout));
  Part_1__1_bit_Full_Adder part_1_1_bit_full_adder_4 (
    .CarryIn(part_1_1_bit_full_adder_3_carryout), .A(A[3]), .B(B[3]), .Answer(out_4[3]), .CarryOut(CarryOut));
endmodule

module Part_3__4_bit_ALU (
  input  [3:0] A,
  input  [3:0] B,
  input  [3:0] A_2,
  input  [3:0] B_2,
  input  [3:0] A_3,
  input  [3:0] A_4,
  input  [3:0] A_5,
  input  [2:0] in_8,
  input  [3:0] A_6,
  input  [3:0] B_3,
  input  [3:0] A_7,
  input  [3:0] B_4,
  input  [3:0] A_8,
  input  [3:0] B_5,
  output _1__Addition,
  output _2__Subtraction,
  output _3__Decrement,
  output _4__2_s_Negation,
  output [3:0] out_19
);

  wire [3:0] and_1_out, not_1_out, not_2_out, not_3_out, or_1_out, part_2_4_bit_full_adder_1_out_4,
       part_2_4_bit_full_adder_2_out_4, part_2_4_bit_full_adder_3_out_4, part_2_4_bit_full_adder_4_out_4,
       xor_1_out;

  assign not_1_out = ~B_2;  // NOT_Gate not_1, 4 bits wide
  assign not_2_out = ~4'b0000;  // NOT_Gate not_2, 4 bits wide
  assign not_3_out = ~A_4;  // NOT_Gate not_3, 4 bits wide
  Part_2__4_bit_Full_Adder part_2_4_bit_full_adder_1 (
    .CarryIn(1'b0), .A(A), .B(B), .out_4(part_2_4_bit_full_adder_1_out_4), .CarryOut(_1__Addition));
  Part_2__4_bit_Full_Adder part_2_4_bit_full_adder_2 (
    .CarryIn(1'b1), .A(A_2), .B(not_1_out), .out_4(part_2_4_bit_full_adder_2_out_4),
    .CarryOut(_2__Subtraction));
  Part_2__4_bit_Full_Adder part_2_4_bit_full_adder_3 (
    .CarryIn(1'b0), .A(A_3), .B(not_2_out), .out_4(part_2_4_bit_full_adder_3_out_4), .CarryOut(_3__Decrement));
  Part_2__4_bit_Full_Adder part_2_4_bit_full_adder_4 (
    .CarryIn(1'b0), .A(not_3_out), .B(4'b0001), .out_4(part_2_4_bit_full_adder_4_out_4),
    .CarryOut(_4__2_s_Negation));
  assign and_1_out = A_6 & B_3;  // AND_Gate and_1, 4 bits wide
  assign or_1_out = A_7 | B_4;  // OR_Gate or_1, 4 bits wide
  assign xor_1_out = A_8 ^ B_5;  // XOR_Gate xor_1, 4 bits wide
  Multiplexer #(.select(3), .width(4)) multiplexer_1 (
    .in0(part_2_4_bit_full_adder_1_out_4), .in1(part_2_4_bit_full_adder_2_out_4),
    .in2(part_2_4_bit_full_adder_3_out_4), .in3(part_2_4_bit_full_adder_4_out_4), .in4({A_5[1:0], 2'b00}),
    .in5(and_1_out), .in6(or_1_out), .in7(xor_1_out), .out(out_19), .sel(in_8));  // open: en

  // Notes on the sheet:
  //   5. Multiply by 4
  //   6. AND
  //   7. OR
  //   8. XOR
endmodule

module Part_4__16_bit_Full_Adder (
  input  CarryIn,
  input  [15:0] A,
  input  [15:0] B,
  output [15:0] out_4,
  output CarryOut
);

  wire part_2_4_bit_full_adder_1_carryout, part_2_4_bit_full_adder_2_carryout,
       part_2_4_bit_full_adder_3_carryout;

  Part_2__4_bit_Full_Adder part_2_4_bit_full_adder_1 (
    .CarryIn(CarryIn), .A(A[3:0]), .B(B[3:0]), .out_4(out_4[3:0]),
    .CarryOut(part_2_4_bit_full_adder_1_carryout));
  Part_2__4_bit_Full_Adder part_2_4_bit_full_adder_2 (
    .CarryIn(part_2_4_bit_full_adder_1_carryout), .A(A[7:4]), .B(B[7:4]), .out_4(out_4[7:4]),
    .CarryOut(part_2_4_bit_full_adder_2_carryout));
  Part_2__4_bit_Full_Adder part_2_4_bit_full_adder_3 (
    .CarryIn(part_2_4_bit_full_adder_2_carryout), .A(A[11:8]), .B(B[11:8]), .out_4(out_4[11:8]),
    .CarryOut(part_2_4_bit_full_adder_3_carryout));
  Part_2__4_bit_Full_Adder part_2_4_bit_full_adder_4 (
    .CarryIn(part_2_4_bit_full_adder_3_carryout), .A(A[15:12]), .B(B[15:12]), .out_4(out_4[15:12]),
    .CarryOut(CarryOut));
endmodule

module Part_4__16_bit_ALU (
  input  [15:0] A,
  input  [15:0] B,
  input  [15:0] A_2,
  input  [15:0] B_2,
  input  [15:0] A_3,
  input  [15:0] A_4,
  input  [15:0] A_5,
  input  [2:0] in_8,
  input  [15:0] A_6,
  input  [15:0] B_3,
  input  in_11,
  input  in_12,
  input  [15:0] A_7,
  input  in_14,
  input  [15:0] B_4,
  input  in_16,
  input  [15:0] A_8,
  input  in_18,
  input  in_19,
  input  [15:0] B_5,
  output _1__Addition,
  output _2__Subtraction,
  output _3__Decrement,
  output _4__2_s_Negation,
  output [15:0] out_25,
  output out_26
);

  wire and_2_out, and_3_out, and_4_out, and_5_out;
  wire [15:0] and_1_out, not_1_out, not_2_out, not_3_out, or_1_out, part_4_16_bit_full_adder_1_out_4,
       part_4_16_bit_full_adder_2_out_4, part_4_16_bit_full_adder_3_out_4, part_4_16_bit_full_adder_4_out_4,
       xor_1_out;

  assign not_1_out = ~B_2;  // NOT_Gate not_1, 16 bits wide
  assign not_2_out = ~{16{1'b0}};  // NOT_Gate not_2, 16 bits wide
  assign not_3_out = ~A_4;  // NOT_Gate not_3, 16 bits wide
  Part_4__16_bit_Full_Adder part_4_16_bit_full_adder_1 (
    .CarryIn(1'b0), .A(A), .B(B), .out_4(part_4_16_bit_full_adder_1_out_4), .CarryOut(_1__Addition));
  Part_4__16_bit_Full_Adder part_4_16_bit_full_adder_2 (
    .CarryIn(1'b1), .A(A_2), .B(not_1_out), .out_4(part_4_16_bit_full_adder_2_out_4),
    .CarryOut(_2__Subtraction));
  Part_4__16_bit_Full_Adder part_4_16_bit_full_adder_3 (
    .CarryIn(1'b0), .A(A_3), .B(not_2_out), .out_4(part_4_16_bit_full_adder_3_out_4), .CarryOut(_3__Decrement));
  Part_4__16_bit_Full_Adder part_4_16_bit_full_adder_4 (
    .CarryIn(1'b0), .A(not_3_out), .B(16'h1), .out_4(part_4_16_bit_full_adder_4_out_4),
    .CarryOut(_4__2_s_Negation));
  assign and_1_out = A_6 & B_3;  // AND_Gate and_1, 16 bits wide
  assign or_1_out = A_7 | B_4;  // OR_Gate or_1, 16 bits wide
  assign xor_1_out = A_8 ^ B_5;  // XOR_Gate xor_1, 16 bits wide
  Multiplexer #(.select(3), .width(16), .enable("false")) multiplexer_1 (
    .in0(part_4_16_bit_full_adder_1_out_4), .in1(part_4_16_bit_full_adder_2_out_4),
    .in2(part_4_16_bit_full_adder_3_out_4), .in3(part_4_16_bit_full_adder_4_out_4), .in4({A_5[13:0], 2'b00}),
    .in5(and_1_out), .in6(or_1_out), .in7(xor_1_out), .out(out_25), .sel(in_8));
  and and_2 (and_2_out, ~in_11, ~in_18, in_19);  // AND_Gate
  and and_3 (and_3_out, in_12, ~in_18, in_19);  // AND_Gate
  and and_4 (and_4_out, in_14, in_18, ~in_19);  // AND_Gate
  and and_5 (and_5_out, in_16, in_18, in_19);
  or or_2 (out_26, and_2_out, and_3_out, and_4_out, and_5_out);

  // Notes on the sheet:
  //   6. AND
  //   7. OR
  //   8. XOR
  //   5. Multiply by 4
  //   multiplexer
endmodule
